# Fritzing sketch Robot Arm (saved by Fritzing 0.8.7b)

parts:
  Part1 = Arduino Uno (Rev3)  # not connected
  Part2 = Arduino Uno (Rev3)
  SM1 = 28BYJ-48 Stepper Motor [part_number=28BYJ-48]
  Arduino_CNC_Shield_V3_00_1 = Arduino_CNC_V3.00
  SM2 = 28BYJ-48 Stepper Motor [part_number=28BYJ-48]
  Driver1 = 28BYJ-48 Driver Module [part_number=ULN2003 package=THT]
  Driver2 = 28BYJ-48 Driver Module [part_number=ULN2003 package=THT]
  M1 = Stepper Motor - Bipolar
  M2 = Stepper Motor - Bipolar
  M3 = Stepper Motor - Bipolar
  J1 = Basic Servo
  J2 = Power Jack [package=power_jack_combo]

nets:
  N1: Part2.A4/SDA, Arduino_CNC_Shield_V3_00_1.SDA
  N2: Part2.A5/SCL, Arduino_CNC_Shield_V3_00_1.SCL_/_Probe
  N3: Part2.D8, Driver2.IN1
  N4: Part2.D9_PWM, Driver2.IN2
  N5: Part2.D10_PWM/SS, Driver2.IN3
  N6: Part2.D11_PWM/MOSI, Driver2.IN4
  N7: Part2.D3_PWM, J1.pulse
  N8: Part2.D4, Driver1.IN1
  N9: Part2.D5_PWM, Driver1.IN2
  N10: Part2.D6_PWM, Driver1.IN3
  N11: Part2.D7, Driver1.IN4
  5V: Part2.5V, J1.vcc
  GND: Part2.GND, Arduino_CNC_Shield_V3_00_1.GND#76, J1.gnd
  N12: SM1.blue-pin, Driver1.blue-pin
  N13: SM1.pink-pin, Driver1.pink-pin
  N14: SM1.yellow-pin, Driver1.yellow-pin
  N15: SM1.orange-pin, Driver1.orange-pin
  N16: SM1.red-pin, Driver1.red-pin
  N17: Arduino_CNC_Shield_V3_00_1.EN(able), Arduino_CNC_Shield_V3_00_1.GND#2
  N18: Arduino_CNC_Shield_V3_00_1.D12, Arduino_CNC_Shield_V3_00_1.A.STP
  N19: Arduino_CNC_Shield_V3_00_1.A.DIR, Arduino_CNC_Shield_V3_00_1.D13
  GND_2: Arduino_CNC_Shield_V3_00_1.POWER_-, Driver1.GND, Driver2.GND, J2.GNDBREAK
  N20: Arduino_CNC_Shield_V3_00_1.POWER_+, Driver1.Vmotor, Driver2.Vmotor, J2.PWR
  N21: Arduino_CNC_Shield_V3_00_1.X-MTR_'1', M3.C
  N22: Arduino_CNC_Shield_V3_00_1.X-MTR_'2', M3.D
  N23: Arduino_CNC_Shield_V3_00_1.X-MTR_'3', M3.B
  N24: Arduino_CNC_Shield_V3_00_1.X-MTR_'4', M3.A
  N25: Arduino_CNC_Shield_V3_00_1.Z-MTR_'1', M1.C
  N26: Arduino_CNC_Shield_V3_00_1.Z-MTR_'2', M1.D
  N27: Arduino_CNC_Shield_V3_00_1.Z-MTR_'3', M1.B
  N28: Arduino_CNC_Shield_V3_00_1.Z-MTR_'4', M1.A
  N29: Arduino_CNC_Shield_V3_00_1.Y-MTR_'1', M2.C
  N30: Arduino_CNC_Shield_V3_00_1.Y-MTR_'2', M2.D
  N31: Arduino_CNC_Shield_V3_00_1.Y-MTR_'3', M2.B
  N32: Arduino_CNC_Shield_V3_00_1.Y-MTR_'4', M2.A
  N33: SM2.blue-pin, Driver2.blue-pin
  N34: SM2.pink-pin, Driver2.pink-pin
  N35: SM2.yellow-pin, Driver2.yellow-pin
  N36: SM2.orange-pin, Driver2.orange-pin
  N37: SM2.red-pin, Driver2.red-pin

notes:
  12V power source input
  Master UNO
  Slave UNO
  Axis 1
  Axis 2
  Axis 3
  Stepper 2
  Stepper 1
  Gripper
  Connect to power source
  Connect to computer

custom parts:
  28BYJ-48 Stepper Motor: Unipolar Stepper Motor 28BYJ-48 Top coil - pink & orange Bottom coil - blue & yellow Common rail - red Connector pins: blue - pink - yellow - orange - red
  Arduino_CNC_V3.00: Protoneer Arduino CNC Shield V3.00 If using Grbl V0.9: The “A” axis can not be used (yet). The “SCL” (Arduino A5) pin is now used for 'Probing' input. The “End Stops Z+ & Z-” (Arduino D11) and “SpnEn” (Arduino D12) have been switched!
  28BYJ-48 Driver Module: High-power ULN2003 Stepper Motor Driver Board Test Module For Arduino AVR SMD
